// Logisim project MIPS.circ as structural Verilog: 9 circuits, main circuit main
module main (
  input  in_1,
  input  [15:0] in_2,
  input  in_3,
  input  [15:0] in_4,
  input  [3:0] in_5
);

  wire and_or_8bits_1_negative, and_or_8bits_1_zero, and_or_8bits_2_negative, and_or_8bits_2_zero;
  wire [4:0] program_cointer_1_saida;
  wire [15:0] and_or_8bits_1_s, bit_extender_1_out, ledbar_1_p1, rom_1_data;

  program_cointer program_cointer_1 (
    .Entrada(and_or_8bits_1_s[4:0]), .Clock(in_1), .Clear(in_3), .Saida(program_cointer_1_saida));
  assign bit_extender_1_out = {{11{program_cointer_1_saida[4]}}, program_cointer_1_saida};  // Bit_Extender bit_extender_1
  ROM #(.addrWidth(5), .dataWidth(16)) rom_1 (.addr(program_cointer_1_saida), .data(rom_1_data));
  LED led_1 (.in(and_or_8bits_1_zero));
  and_or_8bits and_or_8bits_1 (
    .SEL(4'b0000), .A(16'h1), .B(bit_extender_1_out), .Zero(and_or_8bits_1_zero), .S(and_or_8bits_1_s),
    .Negative(and_or_8bits_1_negative));
  LED led_2 (.in(and_or_8bits_1_negative));
  LED led_3 (.in(and_or_8bits_2_zero));
  // LedBar #(.inputtype("row"), .matrixcols(16)) ledbar_1: pin names not known; wires that end beside it: ledbar_1_p1
  and_or_8bits and_or_8bits_2 (
    .SEL(in_5), .A(in_2), .B(in_4), .Zero(and_or_8bits_2_zero), .S(ledbar_1_p1),
    .Negative(and_or_8bits_2_negative));
  LED led_4 (.in(and_or_8bits_2_negative));
endmodule

module program_cointer (
  input  [4:0] Entrada,
  input  Clock,
  input  Clear,
  output [4:0] Saida
);

  D_Flip_Flop #(.trigger("falling")) d_ff_1 (
    .D(Entrada[4]), .clk(Clock), .Q(Saida[4]), .reset(Clear));  // open: Qn, preset
  D_Flip_Flop #(.trigger("falling")) d_ff_2 (
    .D(Entrada[3]), .clk(Clock), .Q(Saida[3]), .reset(Clear));  // open: Qn, preset
  D_Flip_Flop #(.trigger("falling")) d_ff_3 (
    .D(Entrada[2]), .clk(Clock), .Q(Saida[2]), .reset(Clear));  // open: Qn, preset
  D_Flip_Flop #(.trigger("falling")) d_ff_4 (
    .D(Entrada[1]), .clk(Clock), .Q(Saida[1]), .reset(Clear));  // open: Qn, preset
  D_Flip_Flop #(.trigger("falling")) d_ff_5 (
    .D(Entrada[0]), .clk(Clock), .Q(Saida[0]), .reset(Clear));  // open: Qn, preset
endmodule

module Register_8bits (
  input  [7:0] in_1,
  input  Li,
  input  Ei,
  input  CLR,
  input  CLK,
  output [7:0] out_6
);

  wire controlled_buffer_1_out, controlled_buffer_2_out, controlled_buffer_3_out, controlled_buffer_4_out,
       controlled_buffer_5_out, controlled_buffer_6_out, controlled_buffer_7_out, controlled_buffer_8_out,
       d_ff_1_q, d_ff_2_q, d_ff_3_q, d_ff_4_q, d_ff_5_q, d_ff_6_q, d_ff_7_q, d_ff_8_q;

  D_Flip_Flop #(.trigger("high")) d_ff_1 (
    .D(controlled_buffer_1_out), .clk(CLK), .Q(d_ff_1_q), .reset(CLR));  // open: Qn, preset
  assign controlled_buffer_1_out = Li ? in_1[0] : 1'bz;  // Controlled_Buffer controlled_buffer_1
  D_Flip_Flop #(.trigger("high")) d_ff_2 (
    .D(controlled_buffer_2_out), .clk(CLK), .Q(d_ff_2_q), .reset(CLR));  // open: Qn, preset
  assign controlled_buffer_2_out = Li ? in_1[1] : 1'bz;  // Controlled_Buffer controlled_buffer_2
  D_Flip_Flop #(.trigger("high")) d_ff_3 (
    .D(controlled_buffer_3_out), .clk(CLK), .Q(d_ff_3_q), .reset(CLR));  // open: Qn, preset
  assign controlled_buffer_3_out = Li ? in_1[2] : 1'bz;  // Controlled_Buffer controlled_buffer_3
  D_Flip_Flop #(.trigger("high")) d_ff_4 (
    .D(controlled_buffer_4_out), .clk(CLK), .Q(d_ff_4_q), .reset(CLR));  // open: Qn, preset
  assign controlled_buffer_4_out = Li ? in_1[3] : 1'bz;  // Controlled_Buffer controlled_buffer_4
  D_Flip_Flop #(.trigger("high")) d_ff_5 (
    .D(controlled_buffer_5_out), .clk(CLK), .Q(d_ff_5_q), .reset(CLR));  // open: Qn, preset
  assign controlled_buffer_5_out = Li ? in_1[4] : 1'bz;  // Controlled_Buffer controlled_buffer_5
  D_Flip_Flop #(.trigger("high")) d_ff_6 (
    .D(controlled_buffer_6_out), .clk(CLK), .Q(d_ff_6_q), .reset(CLR));  // open: Qn, preset
  assign controlled_buffer_6_out = Li ? in_1[5] : 1'bz;  // Controlled_Buffer controlled_buffer_6
  D_Flip_Flop #(.trigger("high")) d_ff_7 (
    .D(controlled_buffer_7_out), .clk(CLK), .Q(d_ff_7_q), .reset(CLR));  // open: Qn, preset
  assign controlled_buffer_7_out = Li ? in_1[6] : 1'bz;  // Controlled_Buffer controlled_buffer_7
  D_Flip_Flop #(.trigger("high")) d_ff_8 (
    .D(controlled_buffer_8_out), .clk(CLK), .Q(d_ff_8_q), .reset(CLR));  // open: Qn, preset
  assign controlled_buffer_8_out = Li ? in_1[7] : 1'bz;  // Controlled_Buffer controlled_buffer_8
  assign out_6[0] = Ei ? d_ff_1_q : 1'bz;  // Controlled_Buffer controlled_buffer_9
  assign out_6[1] = Ei ? d_ff_2_q : 1'bz;  // Controlled_Buffer controlled_buffer_10
  assign out_6[2] = Ei ? d_ff_3_q : 1'bz;  // Controlled_Buffer controlled_buffer_11
  assign out_6[3] = Ei ? d_ff_4_q : 1'bz;  // Controlled_Buffer controlled_buffer_12
  assign out_6[4] = Ei ? d_ff_5_q : 1'bz;  // Controlled_Buffer controlled_buffer_13
  assign out_6[5] = Ei ? d_ff_6_q : 1'bz;  // Controlled_Buffer controlled_buffer_14
  assign out_6[6] = Ei ? d_ff_7_q : 1'bz;  // Controlled_Buffer controlled_buffer_15
  assign out_6[7] = Ei ? d_ff_8_q : 1'bz;  // Controlled_Buffer controlled_buffer_16
endmodule

module ALU (
  input  [7:0] INA,
  input  [7:0] INB,
  input  [1:0] Su,
  input  Eu,
  output [7:0] OUT1
);

  wire clock_1_out, not_1_out;
  wire [7:0] and_or_8bits_1_p4, register_8bits_1_out_6;

  Clock clock_1 (.out(clock_1_out));
  Register_8bits register_8bits_1 (
    .in_1(INA), .Li(not_1_out), .Ei(1'b1), .CLK(clock_1_out), .out_6(register_8bits_1_out_6));  // open: CLR
  not not_1 (not_1_out, Eu);
  // and_or_8bits and_or_8bits_1: pin names not known; wires that end beside it: register_8bits_1_out_6, INB, Su, and_or_8bits_1_p4
  assign OUT1 = Eu ? and_or_8bits_1_p4 : 8'bz;  // Controlled_Buffer controlled_buffer_1
endmodule

module somador_1bit (
  input  A,
  input  B,
  input  Cin,
  output Cout,
  output Soma
);

  wire and_1_out, and_2_out, and_3_out, and_4_out, and_5_out, xnor_1_out, xor_1_out;

  and and_1 (and_1_out, A, B);
  and and_2 (and_2_out, A, Cin);
  and and_3 (and_3_out, B, Cin);
  xnor xnor_1 (xnor_1_out, A, B);
  xor xor_1 (xor_1_out, A, B);
  or or_1 (Cout, and_1_out, and_2_out, and_3_out);
  and and_4 (and_4_out, xnor_1_out, Cin);
  and and_5 (and_5_out, xor_1_out, ~Cin);  // AND_Gate
  or or_2 (Soma, and_4_out, and_5_out);
endmodule

module somador_subtrator_1bit (
  input  Cin,
  input  Sub,
  input  A,
  input  B,
  output S,
  output Cout
);

  wire xor_1_out;

  xor xor_1 (xor_1_out, Sub, B);
  somador_1bit somador_1bit_1 (.A(A), .B(xor_1_out), .Cin(Cin), .Cout(Cout), .Soma(S));
endmodule

module somador_subtrator_8bits (
  input  Sub,
  input  [7:0] A,
  input  [7:0] B,
  output [7:0] S,
  output Zero,
  output Negative,
  output Cout
);

  wire somador_subtrator_1bit_1_cout, somador_subtrator_1bit_2_cout, somador_subtrator_1bit_3_cout,
       somador_subtrator_1bit_4_cout, somador_subtrator_1bit_5_cout, somador_subtrator_1bit_6_cout,
       somador_subtrator_1bit_7_cout;

  somador_subtrator_1bit somador_subtrator_1bit_1 (
    .A(A[0]), .B(B[0]), .Sub(Sub), .Cin(Sub), .Cout(somador_subtrator_1bit_1_cout), .S(S[0]));
  somador_subtrator_1bit somador_subtrator_1bit_2 (
    .A(A[1]), .B(B[1]), .Sub(Sub), .Cin(somador_subtrator_1bit_1_cout), .Cout(somador_subtrator_1bit_2_cout),
    .S(S[1]));
  somador_subtrator_1bit somador_subtrator_1bit_3 (
    .A(A[2]), .B(B[2]), .Sub(Sub), .Cin(somador_subtrator_1bit_2_cout), .Cout(somador_subtrator_1bit_3_cout),
    .S(S[2]));
  somador_subtrator_1bit somador_subtrator_1bit_4 (
    .A(A[3]), .B(B[3]), .Sub(Sub), .Cin(somador_subtrator_1bit_3_cout), .Cout(somador_subtrator_1bit_4_cout),
    .S(S[3]));
  somador_subtrator_1bit somador_subtrator_1bit_5 (
    .A(A[4]), .B(B[4]), .Sub(Sub), .Cin(somador_subtrator_1bit_4_cout), .Cout(somador_subtrator_1bit_5_cout),
    .S(S[4]));
  somador_subtrator_1bit somador_subtrator_1bit_6 (
    .A(A[5]), .B(B[5]), .Sub(Sub), .Cin(somador_subtrator_1bit_5_cout), .Cout(somador_subtrator_1bit_6_cout),
    .S(S[5]));
  somador_subtrator_1bit somador_subtrator_1bit_7 (
    .A(A[6]), .B(B[6]), .Sub(Sub), .Cin(somador_subtrator_1bit_6_cout), .Cout(somador_subtrator_1bit_7_cout),
    .S(S[6]));
  somador_subtrator_1bit somador_subtrator_1bit_8 (
    .A(A[7]), .B(B[7]), .Sub(Sub), .Cin(somador_subtrator_1bit_7_cout), .Cout(Cout), .S(Negative));
  and and_1 (Zero, ~S[0], ~S[1], ~S[2], ~S[3], ~S[4], ~S[5], ~S[6]);  // AND_Gate

  assign S[7] = Negative;
endmodule

module and_or_1bit (
  input  A,
  input  B,
  input  Cin,
  input  [3:0] sel,
  output Cout,
  output S
);

  wire and_1_out, nand_1_out, nor_1_out, or_1_out, somador_subtrator_1bit_1_s, xor_1_out;

  somador_subtrator_1bit somador_subtrator_1bit_1 (
    .A(A), .B(B), .Sub(sel[0]), .Cin(Cin), .Cout(Cout), .S(somador_subtrator_1bit_1_s));
  and and_1 (and_1_out, B, A);
  or or_1 (or_1_out, A, B);
  xor xor_1 (xor_1_out, A, B);
  nand nand_1 (nand_1_out, A, B);
  nor nor_1 (nor_1_out, A, B);
  Multiplexer #(.select(4)) multiplexer_1 (
    .in0(somador_subtrator_1bit_1_s), .in1(somador_subtrator_1bit_1_s), .in2(and_1_out), .in3(or_1_out),
    .in4(xor_1_out), .in5(nand_1_out), .in6(nor_1_out), .out(S), .sel(sel));  // open: in7, in8, in9, in10, in11, in12, in13, in14, in15
endmodule

module and_or_8bits (
  input  [3:0] SEL,
  input  [15:0] A,
  input  [15:0] B,
  output [15:0] S,
  output Negative,
  output Zero
);

  wire and_or_1bit_1_cout, and_or_1bit_2_cout, and_or_1bit_3_cout, and_or_1bit_4_cout, and_or_1bit_5_cout,
       and_or_1bit_6_cout, and_or_1bit_7_cout, and_or_1bit_8_cout, and_or_1bit_9_cout, and_or_1bit_10_cout,
       and_or_1bit_11_cout, and_or_1bit_12_cout, and_or_1bit_13_cout, and_or_1bit_14_cout,
       and_or_1bit_15_cout;

  and_or_1bit and_or_1bit_1 (.sel(SEL), .A(A[0]), .B(B[0]), .Cin(SEL[0]), .Cout(and_or_1bit_1_cout), .S(S[0]));
  and_or_1bit and_or_1bit_2 (
    .sel(SEL), .A(A[1]), .B(B[1]), .Cin(and_or_1bit_1_cout), .Cout(and_or_1bit_2_cout), .S(S[1]));
  and_or_1bit and_or_1bit_3 (
    .sel(SEL), .A(A[2]), .B(B[2]), .Cin(and_or_1bit_2_cout), .Cout(and_or_1bit_3_cout), .S(S[2]));
  and_or_1bit and_or_1bit_4 (
    .sel(SEL), .A(A[3]), .B(B[3]), .Cin(and_or_1bit_3_cout), .Cout(and_or_1bit_4_cout), .S(S[3]));
  and_or_1bit and_or_1bit_5 (
    .sel(SEL), .A(A[4]), .B(B[4]), .Cin(and_or_1bit_4_cout), .Cout(and_or_1bit_5_cout), .S(S[4]));
  and_or_1bit and_or_1bit_6 (
    .sel(SEL), .A(A[5]), .B(B[5]), .Cin(and_or_1bit_5_cout), .Cout(and_or_1bit_6_cout), .S(S[5]));
  and_or_1bit and_or_1bit_7 (
    .sel(SEL), .A(A[6]), .B(B[6]), .Cin(and_or_1bit_6_cout), .Cout(and_or_1bit_7_cout), .S(S[6]));
  and_or_1bit and_or_1bit_8 (
    .sel(SEL), .A(A[7]), .B(B[7]), .Cin(and_or_1bit_7_cout), .Cout(and_or_1bit_8_cout), .S(S[7]));
  and_or_1bit and_or_1bit_9 (
    .sel(SEL), .A(A[8]), .B(B[8]), .Cin(and_or_1bit_8_cout), .Cout(and_or_1bit_9_cout), .S(S[8]));
  and_or_1bit and_or_1bit_10 (
    .sel(SEL), .A(A[9]), .B(B[9]), .Cin(and_or_1bit_9_cout), .Cout(and_or_1bit_10_cout), .S(S[9]));
  and_or_1bit and_or_1bit_11 (
    .sel(SEL), .A(A[10]), .B(B[10]), .Cin(and_or_1bit_10_cout), .Cout(and_or_1bit_11_cout), .S(S[10]));
  and_or_1bit and_or_1bit_12 (
    .sel(SEL), .A(A[11]), .B(B[11]), .Cin(and_or_1bit_11_cout), .Cout(and_or_1bit_12_cout), .S(S[11]));
  and_or_1bit and_or_1bit_13 (
    .sel(SEL), .A(A[12]), .B(B[12]), .Cin(and_or_1bit_12_cout), .Cout(and_or_1bit_13_cout), .S(S[12]));
  and_or_1bit and_or_1bit_14 (
    .sel(SEL), .A(A[13]), .B(B[13]), .Cin(and_or_1bit_13_cout), .Cout(and_or_1bit_14_cout), .S(S[13]));
  and_or_1bit and_or_1bit_15 (
    .sel(SEL), .A(A[14]), .B(B[14]), .Cin(and_or_1bit_14_cout), .Cout(and_or_1bit_15_cout), .S(S[14]));
  and_or_1bit and_or_1bit_16 (.sel(SEL), .A(A[15]), .B(B[15]), .Cin(and_or_1bit_15_cout), .S(Negative));  // open: Cout
  nor nor_1 (Zero, S[7], S[0], S[1], S[2], S[3], S[4], S[5], S[6], S[8], S[9], S[10], S[11], S[12], S[13], S[14], Negative);

  assign S[15] = Negative;
endmodule
