// Logisim project ULA.circ as structural Verilog: 5 circuits, main circuit main
module main (
  input  Cin,
  input  A,
  input  B,
  input  [2:0] selecao,
  input  [7:0] A1,
  input  [7:0] B1,
  input  [2:0] Selecao1,
  output saida,
  output Cout
);

  wire saida1_p2, saida1_p3, saida1_p4, saida1_p5, ula_8bits_1_cout;
  wire [7:0] ula_8bits_1_out_4;

  ULA_8bits ula_8bits_1 (.A(A1), .B(B1), .Sel(Selecao1), .Cout(ula_8bits_1_cout), .out_4(ula_8bits_1_out_4));
  ULA_1bit ula_1bit_1 (.A(A), .B(B), .Sel(selecao), .Cin(Cin), .Cout(Cout), .S(saida));
  // LedBar #(.inputtype("row")) saida1: pin names not known; wires that end beside it: ula_8bits_1_out_4, saida1_p2, saida1_p3, saida1_p4, saida1_p5
  LED Cout1 (.in(ula_8bits_1_cout));

  // Notes on the sheet:
  //   ULA de 1 bit
  //    com 8 comandos sendo assim 3 bits de seleção
  //   ULA de 8 bits
  //   é que os dados de entrada e saída é de 8 bits
  //   a ULA segue a mesma tabela de comando a única diferença 
  //   Tabela de comandos
  //   sel
  //   000
  //   001
  //   or
  //   010
  //   011
  //   100
  //   xor
  //   101
  //   110
  //   111
  //   op
  //   and
  //   nand
  //   nor
  //   xnor
  //   add
  //   sub
endmodule

module ULA_1bit (
  input  A,
  input  B,
  input  Cin,
  input  [2:0] Sel,
  output S,
  output Cout
);

  wire and_1_out, and_2_out, and_3_out, nand_1_out, nor_1_out, or_1_out, or_2_out,
       somador_subtrator_1bit_1_cout, somador_subtrator_1bit_1_s, xnor_1_out, xor_1_out;

  and and_1 (and_1_out, ~Sel[0], Sel[1], Sel[2]);  // AND_Gate
  and and_2 (and_2_out, Sel[0], Sel[1], Sel[2]);
  and and_3 (and_3_out, A, B);
  or or_1 (or_1_out, A, B);
  nand nand_1 (nand_1_out, A, B);
  nor nor_1 (nor_1_out, A, B);
  xor xor_1 (xor_1_out, A, B);
  xnor xnor_1 (xnor_1_out, A, B);
  somador_subtrator_1bit somador_subtrator_1bit_1 (
    .A(A), .B(B), .Sub(Sel[0]), .Cin(Cin), .Cout(somador_subtrator_1bit_1_cout),
    .S(somador_subtrator_1bit_1_s));
  or or_2 (or_2_out, and_1_out, and_2_out);
  assign Cout = or_2_out ? somador_subtrator_1bit_1_cout : 1'bz;  // Controlled_Buffer controlled_buffer_1
  Multiplexer #(.select(3)) multiplexer_1 (
    .in0(and_3_out), .in1(or_1_out), .in2(nand_1_out), .in3(nor_1_out), .in4(xor_1_out), .in5(xnor_1_out),
    .in6(somador_subtrator_1bit_1_s), .in7(somador_subtrator_1bit_1_s), .out(S), .sel(Sel));
endmodule

module ULA_8bits (
  input  [7:0] A,
  input  [7:0] B,
  input  [2:0] Sel,
  output [7:0] out_4,
  output Cout
);

  wire ula_1bit_1_cout, ula_1bit_2_cout, ula_1bit_3_cout, ula_1bit_4_cout, ula_1bit_5_cout, ula_1bit_6_cout,
       ula_1bit_7_cout;

  ULA_1bit ula_1bit_1 (.A(A[0]), .B(B[0]), .Sel(Sel), .Cout(ula_1bit_1_cout), .S(out_4[0]));  // open: Cin
  ULA_1bit ula_1bit_2 (.A(A[1]), .B(B[1]), .Sel(Sel), .Cin(ula_1bit_1_cout), .Cout(ula_1bit_2_cout), .S(out_4[1]));
  ULA_1bit ula_1bit_3 (.A(A[2]), .B(B[2]), .Sel(Sel), .Cin(ula_1bit_2_cout), .Cout(ula_1bit_3_cout), .S(out_4[2]));
  ULA_1bit ula_1bit_4 (.A(A[3]), .B(B[3]), .Sel(Sel), .Cin(ula_1bit_3_cout), .Cout(ula_1bit_4_cout), .S(out_4[3]));
  ULA_1bit ula_1bit_5 (.A(A[4]), .B(B[4]), .Sel(Sel), .Cin(ula_1bit_4_cout), .Cout(ula_1bit_5_cout), .S(out_4[4]));
  ULA_1bit ula_1bit_6 (.A(A[5]), .B(B[5]), .Sel(Sel), .Cin(ula_1bit_5_cout), .Cout(ula_1bit_6_cout), .S(out_4[5]));
  ULA_1bit ula_1bit_7 (.A(A[6]), .B(B[6]), .Sel(Sel), .Cin(ula_1bit_6_cout), .Cout(ula_1bit_7_cout), .S(out_4[6]));
  ULA_1bit ula_1bit_8 (.A(A[7]), .B(B[7]), .Sel(Sel), .Cin(ula_1bit_7_cout), .Cout(Cout), .S(out_4[7]));
endmodule

module somador_subtrator_1bit (
  input  Cin,
  input  Sub,
  input  A,
  input  B,
  output S,
  output Cout
);

  wire xor_1_out;

  xor xor_1 (xor_1_out, Sub, B);
  somador_1bit somador_1bit_1 (.A(A), .B(xor_1_out), .Cin(Cin), .Cout(Cout), .Soma(S));
endmodule

module somador_1bit (
  input  A,
  input  B,
  input  Cin,
  output Cout,
  output Soma
);

  wire and_1_out, and_2_out, and_3_out, and_4_out, and_5_out, xnor_1_out, xor_1_out;

  and and_1 (and_1_out, A, B);
  and and_2 (and_2_out, A, Cin);
  and and_3 (and_3_out, B, Cin);
  xnor xnor_1 (xnor_1_out, A, B);
  xor xor_1 (xor_1_out, A, B);
  or or_1 (Cout, and_1_out, and_2_out, and_3_out);
  and and_4 (and_4_out, xnor_1_out, Cin);
  and and_5 (and_5_out, xor_1_out, ~Cin);  // AND_Gate
  or or_2 (Soma, and_4_out, and_5_out);
endmodule
