// Logisim project somadores_e_sutratores.circ as structural Verilog: 7 circuits, main circuit main
module main (
  input  Cin1,
  input  A1,
  input  B1,
  input  Cin2,
  input  [7:0] A2,
  input  [7:0] B2,
  input  sub3,
  input  Cin3,
  input  A3,
  input  B3,
  input  in_11,
  input  [7:0] in_12,
  input  sub4,
  input  [7:0] A4,
  input  [7:0] B4,
  input  in_16,
  input  Sub,
  input  [7:0] in_18,
  input  [7:0] in_19,
  output [7:0] out_20,
  output out_21,
  output out_22,
  output out_23
);

  wire and_1_out, n7_segment_display_2_p1, n7_segment_display_2_p2, n7_segment_display_3_p2,
       n7_segment_display_6_p1, n7_segment_display_6_p2, n7_segment_display_7_p2, n7_segment_display_10_p1,
       n7_segment_display_10_p2, n7_segment_display_11_p2, not_1_out, somador_1bit_1_cout,
       somador_1bit_1_soma, somador_8bits_1_cout, somador_subtrator_1bit_1_cout, somador_subtrator_1bit_1_s,
       somador_subtrator_8bits_1_cout, somador_subtrator_8bits_1_negative, somador_subtrator_8bits_1_zero,
       xnor_1_out, xnor_2_out, xor_1_out;
  wire [6:0] binary_to_bcd_converter_1_p1, p_n_2_not_number_2, soma, stackoverflow_1_out_2,
       stackoverflow_1_out_2_2, stackoverflow_1_out_2_3, stackoverflow_1_out_3, stackoverflow_1_out_3_2,
       stackoverflow_1_out_3_3, stackoverflow_1_out_3_4, stackoverflow_1_out_3_5, stackoverflow_1_out_3_6,
       stackoverflow_1_out_3_7;
  wire [7:0] p_n_3_not_number, somador_8bits_1_out_4, somador_subtrator_8bits_1_s,
       somador_subtrator_8bits_2_s;
  wire [7:7] multiplexer_1_out, p_n_1_not_number, p_n_2_not_number;
  wire [48:0] stackoverflow_2_out_2, stackoverflow_2_out_3;
  wire [48:21] stackoverflow_1_out_2_4;

  _7_Segment_Display u_7_segment_display_1 (.g(in_18[7]));  // open: f, a, b, e, d, c, dp
  // _7_Segment_Display 7_segment_display_2: pin names not known; wires that end beside it: n7_segment_display_2_p1, n7_segment_display_2_p2
  // BCD_to_7_Segment_decoder bcd_to_7_segment_decoder_1: pin names not known
  // Binary_to_BCD_converter binary_to_bcd_converter_1: pin names not known; wires that end beside it: {2'b00, binary_to_bcd_converter_1_p1}, n7_segment_display_2_p1, n7_segment_display_2_p2
  LED led_1 (.in(somador_subtrator_8bits_1_negative));
  LED led_2 (.in(somador_subtrator_8bits_1_zero));
  // _7_Segment_Display 7_segment_display_3: pin names not known; wires that end beside it: n7_segment_display_2_p2, n7_segment_display_3_p2
  // BCD_to_7_Segment_decoder bcd_to_7_segment_decoder_2: pin names not known
  somador_subtrator_1bit somador_subtrator_1bit_1 (
    .A(A3), .B(B3), .Sub(sub3), .Cin(Cin3), .Cout(somador_subtrator_1bit_1_cout),
    .S(somador_subtrator_1bit_1_s));
  somador_subtrator_8bits somador_subtrator_8bits_1 (
    .A(A4), .B(B4), .Sub(sub4), .Cout(somador_subtrator_8bits_1_cout),
    .Negative(somador_subtrator_8bits_1_negative), .S(somador_subtrator_8bits_1_s),
    .Zero(somador_subtrator_8bits_1_zero));
  LedBar #(.matrixcols(9)) Cout_saida4 (
    .led0(somador_subtrator_8bits_1_cout), .led1(somador_subtrator_8bits_1_s[7]),
    .led2(somador_subtrator_8bits_1_s[6]), .led3(somador_subtrator_8bits_1_s[5]),
    .led4(somador_subtrator_8bits_1_s[4]), .led5(somador_subtrator_8bits_1_s[3]),
    .led6(somador_subtrator_8bits_1_s[2]), .led7(somador_subtrator_8bits_1_s[1]),
    .led8(somador_subtrator_8bits_1_s[0]));
  xor xor_1 (xor_1_out, Sub, in_19[7]);
  _7_Segment_Display u_7_segment_display_4 ();  // open: g, f, a, b, e, d, c, dp
  // BCD_to_7_Segment_decoder bcd_to_7_segment_decoder_3: pin names not known; wires that end beside it: n7_segment_display_3_p2
  somador_1bit somador_1bit_1 (.A(A1), .B(B1), .Cin(Cin1), .Cout(somador_1bit_1_cout), .Soma(somador_1bit_1_soma));
  somador_8bits somador_8bits_1 (
    .A(A2), .B(B2), .Cin(Cin2), .Cout(somador_8bits_1_cout), .out_4(somador_8bits_1_out_4));
  LedBar #(.matrixcols(2)) Cout_saida3 (.led0(somador_subtrator_1bit_1_cout), .led1(somador_subtrator_1bit_1_s));
  P_N p_n_1 (.Number(in_18), .InOff(in_18[7]), .Not_number({p_n_1_not_number[7], binary_to_bcd_converter_1_p1}));
  P_N p_n_2 (.Number(in_19), .InOff(in_19[7]), .Not_number({p_n_2_not_number[7], p_n_2_not_number_2}));
  _7_Segment_Display u_7_segment_display_5 (.g(xor_1_out));  // open: f, a, b, e, d, c, dp
  LedBar #(.matrixcols(2)) Cout_Saida1 (.led0(somador_1bit_1_cout), .led1(somador_1bit_1_soma));
  LedBar #(.matrixcols(9)) Cout_saida2 (
    .led0(somador_8bits_1_cout), .led1(somador_8bits_1_out_4[7]), .led2(somador_8bits_1_out_4[6]),
    .led3(somador_8bits_1_out_4[5]), .led4(somador_8bits_1_out_4[4]), .led5(somador_8bits_1_out_4[3]),
    .led6(somador_8bits_1_out_4[2]), .led7(somador_8bits_1_out_4[1]), .led8(somador_8bits_1_out_4[0]));
  // _7_Segment_Display 7_segment_display_6: pin names not known; wires that end beside it: n7_segment_display_6_p1, n7_segment_display_6_p2
  // BCD_to_7_Segment_decoder bcd_to_7_segment_decoder_4: pin names not known
  // Binary_to_BCD_converter binary_to_bcd_converter_2: pin names not known; wires that end beside it: {2'b00, p_n_2_not_number_2}, n7_segment_display_6_p1, n7_segment_display_6_p2
  somador_subtrator_8bits somador_subtrator_8bits_2 (
    .A(in_18), .B(in_19), .Sub(Sub), .Cout(out_21), .Negative(out_22), .S(somador_subtrator_8bits_2_s),
    .Zero(out_23));
  xnor xnor_1 (xnor_1_out, xor_1_out, in_18[7]);
  // _7_Segment_Display 7_segment_display_7: pin names not known; wires that end beside it: n7_segment_display_6_p2, n7_segment_display_7_p2
  _7_Segment_Display u_7_segment_display_8 ();  // open: g, f, a, b, e, d, c, dp
  // BCD_to_7_Segment_decoder bcd_to_7_segment_decoder_5: pin names not known
  // BCD_to_7_Segment_decoder bcd_to_7_segment_decoder_6: pin names not known; wires that end beside it: n7_segment_display_7_p2
  P_N p_n_3 (.Number(somador_subtrator_8bits_2_s), .InOff(1'b1), .Not_number(p_n_3_not_number));
  Multiplexer #(.width(8)) multiplexer_1 (
    .in0(p_n_3_not_number), .in1(somador_subtrator_8bits_2_s), .out({multiplexer_1_out[7], soma}),
    .sel(not_1_out));
  not not_1 (not_1_out, out_22);
  xnor xnor_2 (xnor_2_out, xor_1_out, out_22);
  _7_Segment_Display u_7_segment_display_9 (.g(out_22));  // open: f, a, b, e, d, c, dp
  // LedBar #(.inputtype("row")) ledbar_1: pin names not known; wires that end beside it: {multiplexer_1_out[7], soma}
  and and_1 (and_1_out, ~xnor_2_out, xnor_1_out);  // AND_Gate
  // _7_Segment_Display 7_segment_display_10: pin names not known; wires that end beside it: n7_segment_display_10_p1, n7_segment_display_10_p2
  // BCD_to_7_Segment_decoder bcd_to_7_segment_decoder_7: pin names not known
  // Binary_to_BCD_converter binary_to_bcd_converter_3: pin names not known; wires that end beside it: {2'b00, soma}, n7_segment_display_10_p1, n7_segment_display_10_p2
  // _7_Segment_Display 7_segment_display_11: pin names not known; wires that end beside it: n7_segment_display_10_p2, n7_segment_display_11_p2
  _7_Segment_Display u_7_segment_display_12 ();  // open: g, f, a, b, e, d, c, dp
  // BCD_to_7_Segment_decoder bcd_to_7_segment_decoder_8: pin names not known
  // BCD_to_7_Segment_decoder bcd_to_7_segment_decoder_9: pin names not known; wires that end beside it: n7_segment_display_11_p2
  P_N p_n_4 (.Number(in_12), .InOff(in_11), .Not_number(out_20));
  StackOverflow stackoverflow_1 (
    .in_1(and_1_out),
    .out_2({stackoverflow_1_out_2_4, stackoverflow_1_out_2_3, stackoverflow_1_out_2_2, stackoverflow_1_out_2}),
    .out_3({stackoverflow_1_out_3_7, stackoverflow_1_out_3_6, stackoverflow_1_out_3_5, stackoverflow_1_out_3_4, stackoverflow_1_out_3_3, stackoverflow_1_out_3_2, stackoverflow_1_out_3}));
  DotMatrix #(.matrixcols(16)) dotmatrix_1 (
    .col0(stackoverflow_1_out_2_4[48:42]), .col1(stackoverflow_1_out_2_4[41:35]),
    .col2(stackoverflow_1_out_2_4[34:28]), .col3(stackoverflow_1_out_2_4[27:21]),
    .col4(stackoverflow_1_out_2_3), .col5({7{1'b0}}), .col6(stackoverflow_1_out_2_2),
    .col7(stackoverflow_1_out_2), .col8(stackoverflow_1_out_3_7), .col9(stackoverflow_1_out_3_6),
    .col10(stackoverflow_1_out_3_5), .col11({7{1'b0}}), .col12(stackoverflow_1_out_3_4),
    .col13(stackoverflow_1_out_3_3), .col14(stackoverflow_1_out_3_2), .col15(stackoverflow_1_out_3));
  DotMatrix #(.matrixcols(16)) dotmatrix_2 (
    .col0(stackoverflow_2_out_2[48:42]), .col1(stackoverflow_2_out_2[41:35]),
    .col2(stackoverflow_2_out_2[34:28]), .col3(stackoverflow_2_out_2[27:21]),
    .col4(stackoverflow_2_out_2[20:14]), .col6(stackoverflow_2_out_2[13:7]),
    .col7(stackoverflow_2_out_2[6:0]), .col8(stackoverflow_2_out_3[48:42]),
    .col9(stackoverflow_2_out_3[41:35]), .col10(stackoverflow_2_out_3[34:28]),
    .col12(stackoverflow_2_out_3[27:21]), .col13(stackoverflow_2_out_3[20:14]),
    .col14(stackoverflow_2_out_3[13:7]), .col15(stackoverflow_2_out_3[6:0]));  // open: col5, col11
  StackOverflow stackoverflow_2 (.in_1(in_16), .out_2(stackoverflow_2_out_2), .out_3(stackoverflow_2_out_3));

  // Notes on the sheet:
  //   (
  //   o Cin nesse CI não foi utilizado, pois está internamente conectado com o sub
  //   )
  //   somador completo de 1 bit
  //   somador completo de 8 bits
  //   somador/subtrator de 1 bit
  //   somador/subtrator de 8 bits
  //   (
  //   +
  //   e também para saber se a saída é zero ou não
  //   representados por LEDs (not e zero respctivamente)
  //   sub = 0 -> adição
  //   sub = 1 -> subtração
  //   esse CI possui indicadores para saber se a saída é negativa ou não
  //   Para uma melhor vizualização segue abaixo o mesmo circuito, porém agora com vizualização de displays indicando soma ou subtração
  //   )
  //   =
  //   de LED indicando Stack Overflow
  //   Tabela verdade somador completo
  //   Entradas | Saídas
  //   ________________
  //   A B Cin | Cout  S
  //   0   0   0 |  0        0
  //   0   0   1 |  0        1
  //   0   1   0 |  0        1
  //   0   1   1 |  1        0
  //   1   0   0 |  0        1
  //   1   0   1 |  1        0
  //   1   1   0 |  1        0
  //   1   1   1 |  1        1
  //   Tabela verdade subtrator completo
  //   Entradas | Saídas
  //   ________________
  //   A B Cin | Cout  S
  //   0   0   0 |  0        0
  //   0   0   1 |  1        1
  //   0   1   0 |  1        1
  //   0   1   1 |  0        1
  //   1   0   0 |  1        0
  //   1   0   1 |  0        0
  //   1   1   0 |  0        0
  //   1   1   1 |  1        1
  //   P_N
  //   esse circuito inverte um numero utilizando-se o ocomplemento de 2
  //   StackOverflow
  //   caso receba 1 na entrada receberá na saída
  //   uma sequencia binária que ascende o painel
  //   Circuitos utilizados nessa biblioteca
  //   indica se inverte ou não
  //   esse painel indica Stack Overflow, ou seja.
  //   se ativado significa que a saída possui um
  //    número que precisa de mais de 8 bits para ser representado
  //   e por isso pode apresentar algum erro nos displays que representam a saída
endmodule

module somador_1bit (
  input  A,
  input  B,
  input  Cin,
  output Cout,
  output Soma
);

  wire and_1_out, and_2_out, and_3_out, and_4_out, and_5_out, xnor_1_out, xor_1_out;

  and and_1 (and_1_out, A, B);
  and and_2 (and_2_out, A, Cin);
  and and_3 (and_3_out, B, Cin);
  xnor xnor_1 (xnor_1_out, A, B);
  xor xor_1 (xor_1_out, A, B);
  or or_1 (Cout, and_1_out, and_2_out, and_3_out);
  and and_4 (and_4_out, xnor_1_out, Cin);
  and and_5 (and_5_out, xor_1_out, ~Cin);  // AND_Gate
  or or_2 (Soma, and_4_out, and_5_out);
endmodule

module somador_8bits (
  input  Cin,
  input  [7:0] A,
  input  [7:0] B,
  output [7:0] out_4,
  output Cout
);

  wire somador_1bit_1_cout, somador_1bit_2_cout, somador_1bit_3_cout, somador_1bit_4_cout,
       somador_1bit_5_cout, somador_1bit_6_cout, somador_1bit_7_cout;

  somador_1bit somador_1bit_1 (.A(A[0]), .B(B[0]), .Cin(Cin), .Cout(somador_1bit_1_cout), .Soma(out_4[0]));
  somador_1bit somador_1bit_2 (
    .A(A[1]), .B(B[1]), .Cin(somador_1bit_1_cout), .Cout(somador_1bit_2_cout), .Soma(out_4[1]));
  somador_1bit somador_1bit_3 (
    .A(A[2]), .B(B[2]), .Cin(somador_1bit_2_cout), .Cout(somador_1bit_3_cout), .Soma(out_4[2]));
  somador_1bit somador_1bit_4 (
    .A(A[3]), .B(B[3]), .Cin(somador_1bit_3_cout), .Cout(somador_1bit_4_cout), .Soma(out_4[3]));
  somador_1bit somador_1bit_5 (
    .A(A[4]), .B(B[4]), .Cin(somador_1bit_4_cout), .Cout(somador_1bit_5_cout), .Soma(out_4[4]));
  somador_1bit somador_1bit_6 (
    .A(A[5]), .B(B[5]), .Cin(somador_1bit_5_cout), .Cout(somador_1bit_6_cout), .Soma(out_4[5]));
  somador_1bit somador_1bit_7 (
    .A(A[6]), .B(B[6]), .Cin(somador_1bit_6_cout), .Cout(somador_1bit_7_cout), .Soma(out_4[6]));
  somador_1bit somador_1bit_8 (.A(A[7]), .B(B[7]), .Cin(somador_1bit_7_cout), .Cout(Cout), .Soma(out_4[7]));
endmodule

module somador_subtrator_1bit (
  input  Cin,
  input  Sub,
  input  A,
  input  B,
  output S,
  output Cout
);

  wire xor_1_out;

  xor xor_1 (xor_1_out, Sub, B);
  somador_1bit somador_1bit_1 (.A(A), .B(xor_1_out), .Cin(Cin), .Cout(Cout), .Soma(S));
endmodule

module somador_subtrator_8bits (
  input  Sub,
  input  [7:0] A,
  input  [7:0] B,
  output [7:0] S,
  output Zero,
  output Negative,
  output Cout
);

  wire somador_subtrator_1bit_1_cout, somador_subtrator_1bit_2_cout, somador_subtrator_1bit_3_cout,
       somador_subtrator_1bit_4_cout, somador_subtrator_1bit_5_cout, somador_subtrator_1bit_6_cout,
       somador_subtrator_1bit_7_cout;

  somador_subtrator_1bit somador_subtrator_1bit_1 (
    .A(A[0]), .B(B[0]), .Sub(Sub), .Cin(Sub), .Cout(somador_subtrator_1bit_1_cout), .S(S[0]));
  somador_subtrator_1bit somador_subtrator_1bit_2 (
    .A(A[1]), .B(B[1]), .Sub(Sub), .Cin(somador_subtrator_1bit_1_cout), .Cout(somador_subtrator_1bit_2_cout),
    .S(S[1]));
  somador_subtrator_1bit somador_subtrator_1bit_3 (
    .A(A[2]), .B(B[2]), .Sub(Sub), .Cin(somador_subtrator_1bit_2_cout), .Cout(somador_subtrator_1bit_3_cout),
    .S(S[2]));
  somador_subtrator_1bit somador_subtrator_1bit_4 (
    .A(A[3]), .B(B[3]), .Sub(Sub), .Cin(somador_subtrator_1bit_3_cout), .Cout(somador_subtrator_1bit_4_cout),
    .S(S[3]));
  somador_subtrator_1bit somador_subtrator_1bit_5 (
    .A(A[4]), .B(B[4]), .Sub(Sub), .Cin(somador_subtrator_1bit_4_cout), .Cout(somador_subtrator_1bit_5_cout),
    .S(S[4]));
  somador_subtrator_1bit somador_subtrator_1bit_6 (
    .A(A[5]), .B(B[5]), .Sub(Sub), .Cin(somador_subtrator_1bit_5_cout), .Cout(somador_subtrator_1bit_6_cout),
    .S(S[5]));
  somador_subtrator_1bit somador_subtrator_1bit_7 (
    .A(A[6]), .B(B[6]), .Sub(Sub), .Cin(somador_subtrator_1bit_6_cout), .Cout(somador_subtrator_1bit_7_cout),
    .S(S[6]));
  somador_subtrator_1bit somador_subtrator_1bit_8 (
    .A(A[7]), .B(B[7]), .Sub(Sub), .Cin(somador_subtrator_1bit_7_cout), .Cout(Cout), .S(Negative));
  and and_1 (Zero, ~S[0], ~S[1], ~S[2], ~S[3], ~S[4], ~S[5], ~S[6]);  // AND_Gate

  assign S[7] = Negative;
endmodule

module P_N (
  input  InOff,
  input  [7:0] Number,
  output [7:0] Not_number
);

  wire [7:0] not_1_out, somador_8bits_1_out_4;

  assign not_1_out = ~Number;  // NOT_Gate not_1, 8 bits wide
  somador_8bits somador_8bits_1 (.A(not_1_out), .Cin(1'b1), .out_4(somador_8bits_1_out_4));  // open: B, Cout
  Multiplexer #(.width(8)) multiplexer_1 (.in0(Number), .in1(somador_8bits_1_out_4), .out(Not_number), .sel(InOff));
endmodule

module StackOverflow (
  input  in_1,
  output [48:0] out_2,
  output [48:0] out_3
);

  assign out_2 = in_1 ? 49'hca4c99299f41 : 49'bz;  // Controlled_Buffer controlled_buffer_1
  assign out_3 = in_1 ? 49'h1060beff22440 : 49'bz;  // Controlled_Buffer controlled_buffer_2
endmodule
